// Logisim project AddMachine.circ as structural Verilog: 1 circuit, main circuit main
module main (
  input  in_1,
  input  in_2,
  input  in_3,
  input  in_4,
  input  in_5,
  input  in_6,
  input  in_7,
  input  in_8,
  output out_9,
  output out_10,
  output out_11,
  output out_12,
  output out_13,
  output out_14,
  output out_15,
  output out_16
);

  wire clock_1_out;
  wire [7:0] adder_1_out;

  Clock clock_1 (.out(clock_1_out));
  Register register_1 (
    .D(adder_1_out), .Q({out_16, out_15, out_14, out_13, out_12, out_11, out_10, out_9}), .clk(clock_1_out));  // open: en, clr
  Adder adder_1 (
    .a({out_16, out_15, out_14, out_13, out_12, out_11, out_10, out_9}),
    .b({in_8, in_7, in_6, in_5, in_4, in_3, in_2, in_1}), .out(adder_1_out));  // open: cin, cout
endmodule
