// Logisim project 第一题.circ as structural Verilog: 1 circuit, main circuit main
module main (
  input  in_1,
  input  in_2,
  input  in_3,
  input  in_4,
  input  in_5,
  input  in_6,
  input  \A_0时选择 ,
  input  in_8,
  input  \B_1_时选择 ,
  input  \控制低位 ,
  input  \二进制高位 ,
  input  \_00时选择 ,
  input  \_01时选择 ,
  input  \_10时选择 ,
  input  in_15,
  output out_16,
  output out_17,
  output out_18,
  output out_19,
  output out_20
);

  wire and_1_out, and_2_out, and_3_out, and_4_out, and_5_out, and_6_out, and_7_out, and_8_out, and_9_out,
       and_10_out, and_11_out, and_12_out, and_13_out, not_1_out, not_2_out, not_3_out, not_4_out, not_6_out,
       not_7_out, not_8_out, or_2_out, or_3_out, or_4_out;

  not not_1 (not_1_out, in_5);
  not not_2 (not_2_out, in_8);
  not not_3 (not_3_out, \二进制高位 );
  not not_4 (not_4_out, \二进制高位 );
  and and_1 (and_1_out, in_1, in_3);
  not not_5 (out_16, and_1_out);
  and and_2 (and_2_out, not_1_out, in_8, in_8);
  and and_3 (and_3_out, in_5, not_2_out);
  and and_4 (and_4_out, not_3_out, \_00时选择 );
  and and_5 (and_5_out, not_4_out, \_01时选择 );
  and and_6 (and_6_out, \二进制高位 , \_10时选择 );
  and and_7 (and_7_out, \二进制高位 , in_15);
  or or_1 (out_18, and_2_out, and_3_out);
  not not_6 (not_6_out, \控制低位 );
  not not_7 (not_7_out, \控制低位 );
  and and_8 (and_8_out, not_6_out, and_4_out);
  and and_9 (and_9_out, and_5_out, \控制低位 );
  and and_10 (and_10_out, and_6_out, not_7_out, not_7_out);
  and and_11 (and_11_out, and_7_out, \控制低位 );
  or or_2 (or_2_out, and_8_out, and_9_out);
  or or_3 (or_3_out, and_10_out, and_11_out);
  or or_4 (or_4_out, in_2, in_4);
  not not_8 (not_8_out, in_6);
  not not_9 (out_17, or_4_out);
  or or_5 (out_20, or_2_out, or_3_out);
  and and_12 (and_12_out, not_8_out, \A_0时选择 );
  and and_13 (and_13_out, \B_1_时选择 , in_6);
  or or_6 (out_19, and_12_out, and_13_out);

  // Notes on the sheet:
  //   （1）NAND
  //   （3）XOR
  //                       （5） 4-to-1MUX
  //   11时选择
  //             （4）2-to-1 MUX
  //   （2）NOR
endmodule
